// Logisim project FA.circ as structural Verilog: 1 circuit, main circuit main
module main (
  input  A,
  input  B,
  input  Ci,
  output Co,
  output Q
);

  wire AND1_2_out, AND1_out, XOR1_out;

  xor XOR1 (XOR1_out, A, B);
  and AND1 (AND1_out, A, B);
  xor XOR1_2 (Q, XOR1_out, Ci);
  and AND1_2 (AND1_2_out, XOR1_out, Ci);
  xor xor_1 (Co, AND1_2_out, AND1_out);
endmodule
