// Logisim project HA.circ as structural Verilog: 1 circuit, main circuit main
module main (
  input  A,
  input  B,
  output Co,
  output Q
);

  xor XOR1 (Q, A, B);
  and AND1 (Co, A, B);
endmodule
